# Fritzing sketch DuePCB (saved by Fritzing 1.0.7)
breadboards: 1

parts:
  Part1 = Arduino Due (Rev2b)
  Seatalk = Camdenboss CTB0158-3 [part_number=CTB0158-3 package=THT]
  U1 = Sharp PC817 [package=THT]
  IC1 = IC, DIP package, 14 pins [chip_label=SN74LS07N]
  J1 = JST-03JQ-BT [part_number=JST-JQ-BT package=THT]
  VR1 = LM2596 (TO220) [part_number=LM2596 package="TO220 [THT]"]
  F1 = FUSE [package=fuse_5mm]
  C1 = Electrolytic Capacitor [capacitance=0.1mF voltage=35V package="100 mil [THT, electrolytic]"]
  L1 = Inductor [package="400 mil [THT]"]
  1N5822 = Rectifier Diode [part_number=1N5822 package="300 mil [THT]"]
  C2 = Electrolytic Capacitor [capacitance=0.22mF voltage=35V package="100 mil [THT, electrolytic]"]
  R1 = Resistor [tolerance=±5% power=0.25W resistance=47k package=THT]
  R2 = Resistor [tolerance=±5% power=0.25W resistance=10k package=THT]
  R3 = Resistor [tolerance=±5% power=0.25W resistance=10k package=THT]
  R4 = Resistor [tolerance=±5% power=0.25W resistance=10k package=THT]
  R5 = Resistor [tolerance=±5% power=0.25W resistance=1k package=THT]
  LED1 = LED - 5mm [color="Red (633nm)" current=0.030A package="5 mm [THT]"]  # not connected
  D1 = Rectifier Diode [part_number=1N4001 package="300 mil [THT]"]
  R6 = Resistor [tolerance=±5% power=0.25W resistance=4.7k package=THT]
  R7 = Resistor [tolerance=±5% power=0.25W resistance=10k package=THT]

nets:
  N1: Part1.D16/TX2, J1.pin1
  N2: Part1.D17/RX2, J1.pin3
  N3: Part1.D18/TX1, R5.Pin_1
  N4: Part1.D19/RX1, Part1.D22, U1.Pin_3, R7.Pin_1
  N5: Part1.IOREF, U1.Pin_4, R4.Pin_1
  N6: Part1.5V, IC1.pin14
  N7: Part1.GND, Seatalk.pin3, U1.Pin_2, IC1.pin7, J1.pin2, VR1.Pin_3, VR1.Pin_5, VR1.Tab, C1.-, 1N5822.anode, C2.-, R3.Pin_0, D1.cathode, R7.Pin_0
  N8: Part1.VIN, L1.pin_0, C2.+, R1.Pin_1
  N9: Seatalk.pin1, F1.2
  N10: Seatalk.pin2, IC1.pin2, R6.Pin_1
  N11: U1.Pin_1, D1.anode
  N12: IC1.pin1, R4.Pin_0, R5.Pin_0
  N13: VR1.Pin_1, F1.1, C1.+
  N14: VR1.Pin_2, L1.pin_1, 1N5822.cathode
  N15: VR1.pin_4, R2.Pin_0, R3.Pin_1
  N16: R1.Pin_0, R2.Pin_1
